# Fritzing sketch schema (saved by Fritzing 0.9.4)
circuit board: 8.46667cm x 5.64444cm
breadboards: 1

parts:
  Raspberry_Pi = Raspberry Pi 2
  Power_plug1 = Power plug
  U1 = WS2812 RGB LED strip
  U2 = 74AHCT125 [part_number=SN74AHCT125 package=dil14]
  U3 = WS2812 RGB LED strip

nets:
  N1: Raspberry_Pi.GPIO21, U2.1A
  GND: Raspberry_Pi.GND, Power_plug1.GND, U1.GND, U2.1OE, U2.2OE, U2.GND, U3.GND
  N2: Raspberry_Pi.GPIO18, U2.2A
  VCC: Raspberry_Pi.5V, Power_plug1.VCC, U1.VCC, U2.VCC, U3.VCC
  N3: U1.DIN, U2.1Y
  N4: U2.2Y, U3.DIN

custom parts:
  WS2812 RGB LED strip: WS2812 strip
  74AHCT125: Quad Level-Shifter (3V to 5V) Quadruple Bus Buffer Gates With 3-State Outputs
